# Fritzing sketch silvia_brew_control (saved by Fritzing 0.9.3b)
breadboards: 1

parts:
  Part1 = Arduino Uno (Rev3)
  Raspberry_Pi_Zero1 = Raspberry Pi Zero
  D2425D1 = Crydom D2425D
  R3 = Resistor [tolerance=±5% resistance=10k package=THT]
  Brew_Switch = SPST Switch [package=r_sw_th]

nets:
  N1: Part1.A4/SDA, Raspberry_Pi_Zero1.GPIO2
  N2: Part1.A5/SCL, Raspberry_Pi_Zero1.GPIO3
  N3: Part1.D12/MISO, D2425D1.A+, D2425D1.B+, R3.Pin_1
  GND: Part1.GND, Raspberry_Pi_Zero1.GND, R3.Pin_0
  N4: Part1.5V, D2425D1.A-, D2425D1.B-, Brew_Switch.P
  N5: Raspberry_Pi_Zero1.GIPO27, Brew_Switch.O

notes:
  SDA
  SCL
  Live
  Solenoid
  Neutral
  Pump

custom parts:
  Crydom D2425D: Crydom dual solid state relay Input 4-15 VDC Output 120/240 VAC 25A
