# Fritzing sketch silvia_oled_display (saved by Fritzing 0.9.3b)
breadboards: 1

parts:
  Part1 = Arduino Uno (Rev3)
  Raspberry_Pi_Zero1 = Raspberry Pi Zero
  OLED1 = OLED 128x64 I2C Monochrome Display

nets:
  N1: Part1.A4/SDA, Raspberry_Pi_Zero1.GPIO2, OLED1.SDA
  N2: Part1.A5/SCL, Raspberry_Pi_Zero1.GPIO3, OLED1.SCK
  GND: Part1.GND, Raspberry_Pi_Zero1.GND, OLED1.GND
  3V3: Raspberry_Pi_Zero1.3v3, OLED1.VDD

notes:
  SDA
  SCL
  3.3V
