# Fritzing sketch silvia_power_control (saved by Fritzing 0.9.3b)
breadboards: 1

parts:
  Part1 = Arduino Uno (Rev3)
  Power_Switch = SPST Switch [package=r_sw_th]
  Raspberry_Pi_1 = Raspberry Pi 3 [part_number=RPI-3-V1.2]
  Q2 = Basic FET N-Channel [part_number=IRF520 package="TO220 [THT]"]
  R4 = Resistor [tolerance=±5% resistance=1k package=THT]
  OMRON1 = OMRON PCB Power Relay – G5LE [part_number=Relay package=THT]

nets:
  N1: Part1.D9_PWM, R4.Pin_1
  GND: Part1.GND, Power_Switch.P, Raspberry_Pi_1.GND, Q2.source
  N2: Part1.VIN, OMRON1.COIL1
  N3: Power_Switch.O, Raspberry_Pi_1.GIPO17, Raspberry_Pi_1.ID_SC
  N4: Q2.gate, R4.Pin_0
  N5: Q2.drain, OMRON1.COIL2

notes:
  Live In
  Relay
  Live Out
  G D S
  IRF520
  12V
