# Fritzing sketch silvia_power_supply (saved by Fritzing 0.9.3b)

parts:
  Part1 = Arduino Uno (Rev3)
  Raspberry_Pi_Zero1 = Raspberry Pi Zero
  U2 = Mini-360 DC-DC Buck converter [package=THT]

nets:
  N1: Part1.A4/SDA, Raspberry_Pi_Zero1.GPIO2
  N2: Part1.A5/SCL, Raspberry_Pi_Zero1.GPIO3
  N3: Part1.GND, U2.IN-
  N4: Part1.VIN, U2.IN+

notes:
  SDA
  SCL
  Power Supply
  12V
  5V
  USB

custom parts:
  Mini-360 DC-DC Buck converter: Mini-360 DC-DC Buck converter. Tiny buck step down voltage converter, input voltage 4.75 to 23V output 1 to 17V adjustable. Available from ebay and the like.
