# Fritzing sketch silvia_scale (saved by Fritzing 0.9.3b)
breadboards: 1

parts:
  OLED1 = OLED 128x64 I2C Monochrome Display
  U1 = NodeMCU V3.0
  S1 = JOYSTICK_MINI [package=joystick_mini]
  Part1 = HX711 Weighing Sensor Module
  Load_Cell1 = Load Cell - Red/white/black/green

nets:
  GND: OLED1.GND, U1.GND#6, U1.GND#13, U1.GND#16, U1.GND#33, S1.GND, Part1.GND
  VDD: OLED1.VDD, U1.3V3, Part1.VCC
  N1: OLED1.SCK, U1.D2
  N2: OLED1.SDA, U1.D1
  N3: U1.D3, S1.LEFT
  N4: U1.D4, Part1.DO/RX
  N5: U1.D5, S1.UP
  N6: U1.D6, S1.DOWN
  N7: U1.D7, S1.CENT
  N8: U1.D8, Part1.CK/TX
  N9: U1.RST, S1.RIGHT
  N10: Part1.E+, Load_Cell1.wire1
  N11: Part1.E-, Load_Cell1.wire2
  N12: Part1.A+, Load_Cell1.wire3
  N13: Part1.A-, Load_Cell1.wire4

custom parts:
  NodeMCU V3.0: ESP8266 based NodeMCU
  Load Cell - Red/white/black/green: A rectangle load cell/weighting pressure Sensor with four wires - Red, white, black, green. Normally corresponding with E+, E-, A+, A- respectively.
