# Fritzing sketch silvia_temperature_control (saved by Fritzing 0.9.3b)
breadboards: 1

parts:
  SSR1 = Generic SSR
  Part1 = Arduino Uno (Rev3)
  Raspberry_Pi_Zero1 = Raspberry Pi Zero
  LM35DT1 = LM35DT [package="TO220 [THT]"]
  R1 = Resistor [tolerance=±5% resistance=10k package=THT]

nets:
  N1: SSR1.input+, Part1.D13/SCK, R1.Pin_0
  N2: SSR1.Input-, Part1.5V, LM35DT1.+Vs
  N3: Part1.A0, LM35DT1.GND
  N4: Part1.A4/SDA, Raspberry_Pi_Zero1.GPIO2
  N5: Part1.A5/SCL, Raspberry_Pi_Zero1.GPIO3
  N6: Part1.GND, LM35DT1.Vout, R1.Pin_1

notes:
  SDA
  SCL
  Live
  Heater

custom parts:
  Generic SSR: Generic solid state relay. Input 3-32VDC Output 24-440VAC 25A
  LM35DT: A LM35 temperature sensor with a temperature range from -55°C to 150°C.
