# Fritzing sketch silvia (saved by Fritzing 0.9.3b)
breadboards: 1

parts:
  Part1 = Arduino Uno (Rev3)
  Raspberry_Pi_Zero1 = Raspberry Pi Zero
  R1 = Resistor [tolerance=±5% resistance=1k package=THT]
  J1 = Power Jack [package=power_jack_smd]
  Q1 = Basic FET N-Channel [part_number=IRF520 package="TO220 [THT]"]
  S1 = SPST Switch [package=r_sw_th]
  T1 = TMP36 Temperature Sensor [thermistor_type=NTC part_number=LM35DT package="TO92 [THT]"]
  U1 = Mini-360 DC-DC Buck converter [package=THT]
  Part2 = HX711 Weighing Sensor Module
  U2 = RELAY-SOLIDSTATE [package=relay-s108t02]
  R2 = Resistor [tolerance=±5% resistance=10k package=THT]
  S2 = SPST Switch [package=r_sw_th]

nets (from the breadboard view):
  N1: Part1.A0, T1.GND
  N2: Part1.A4/SDA, Raspberry_Pi_Zero1.GPIO2
  N3: Part1.A5/SCL, Raspberry_Pi_Zero1.GPIO3
  N4: Part1.D9_PWM, R1.Pin_0, Q1.gate
  N5: Part1.D13/SCK, U2.T1, R2.Pin_0
  N6: Part1.D4, Part2.DO/RX
  N7: Part1.D5_PWM, Part2.CK/TX
  5V: Part1.5V, S1.O, T1.+Vs, Part2.VCC, S2.O
  GND: Part1.GND, Raspberry_Pi_Zero1.GND, R1.Pin_1, J1.GNDBREAK, Q1.source, T1.Vout, U1.IN-, U1.OUT-, Part2.GND, U2.T2, R2.Pin_1
  VIN: Part1.VIN, J1.GND, U1.IN+
  N8: Raspberry_Pi_Zero1.GIPO17, S1.P
  N9: Raspberry_Pi_Zero1.GIPO27, S2.P
  N10: Raspberry_Pi_Zero1.5V, U1.OUT+

notes:
  G D S
  IRF520
  SDA
  SCL
  RELAY
  Power
  Brew

custom parts:
  Mini-360 DC-DC Buck converter: Mini-360 DC-DC Buck converter. Tiny buck step down voltage converter, input voltage 4.75 to 23V output 1 to 17V adjustable. Available from ebay and the like.
